// Logisim project automatic_street_light.circ as structural Verilog: 1 circuit, main circuit main
module main (
  input  DAY_SENSOR,
  input  MOTION_SENSOR,
  input  SYSTEM_ENABLE,
  output STREET_LIGHT
);

  wire not_1_out, or_1_out, undriven;

  not not_1 (not_1_out, DAY_SENSOR);
  // OR_Gate or_1 has open pins: out=or_1_out
  and and_1 (STREET_LIGHT, or_1_out, SYSTEM_ENABLE);
  LED STREET_LIGHT_LED (.in(undriven));
endmodule
